# Fritzing sketch Otis Lite Breadboard (saved by Fritzing 1.0.5)
breadboards: 1

parts:
  S2 = Pushbutton [package="[THT]"]
  S3 = Pushbutton [package="[THT]"]
  LED1 = smd LED [color="Red (633nm)" package="1206 [SMD]"]
  R4 = Resistor [tolerance=±5% resistance=150 package="2010 [SMD]"]
  Pico/Pico2_Mod_2 = Raspberry Pi Pico or Pico 2
  R5 = Resistor [tolerance=±5% resistance=10k package="2010 [SMD]"]
  R6 = Resistor [tolerance=±5% resistance=10k package="2010 [SMD]"]
  R7 = Resistor [tolerance=±5% resistance=10k package="2010 [SMD]"]
  LED2 = smd LED [color="Red (633nm)" package="1206 [SMD]"]
  R8 = Resistor [tolerance=±5% resistance=150 package="2010 [SMD]"]
  S4 = Pushbutton [package="[THT]"]
  LED3 = smd LED [color="Red (633nm)" package="1206 [SMD]"]
  LED4 = smd LED [color="Red (633nm)" package="1206 [SMD]"]
  R9 = Resistor [tolerance=±5% resistance=150 package="2010 [SMD]"]
  R10 = Resistor [tolerance=±5% resistance=150 package="2010 [SMD]"]

nets:
  N1: S2.Pin_1, S2.Pin_2, Pico/Pico2_Mod_2.pin_20, R5.Pin_0
  N2: S2.Pin_3, S2.Pin_4, S3.Pin_3, S3.Pin_4, Pico/Pico2_Mod_2.pin_36, R5.Pin_1, R6.Pin_1, R7.Pin_1, S4.Pin_3, S4.Pin_4
  N3: S3.Pin_1, S3.Pin_2, Pico/Pico2_Mod_2.pin_17, R7.Pin_0
  N4: LED1.cathode, Pico/Pico2_Mod_2.pin_3, Pico/Pico2_Mod_2.pin_8, Pico/Pico2_Mod_2.pin_13, Pico/Pico2_Mod_2.pin_18, Pico/Pico2_Mod_2.pin_23, Pico/Pico2_Mod_2.pin_28, Pico/Pico2_Mod_2.pin_33, Pico/Pico2_Mod_2.pin_38, LED2.cathode, LED3.cathode, LED4.cathode
  N5: LED1.anode, R4.Pin_0
  N6: R4.Pin_1, Pico/Pico2_Mod_2.pin_21
  N7: Pico/Pico2_Mod_2.pin_19, R6.Pin_0, S4.Pin_1, S4.Pin_2
  N8: Pico/Pico2_Mod_2.pin_22, R8.Pin_1
  N9: Pico/Pico2_Mod_2.pin_24, R9.Pin_1
  N10: Pico/Pico2_Mod_2.pin_25, R10.Pin_1
  N11: LED2.anode, R8.Pin_0
  N12: LED3.anode, R9.Pin_0
  N13: LED4.anode, R10.Pin_0

notes:
  Left Button
  Right Button
  Mode Button

custom parts:
  Raspberry Pi Pico or Pico 2: Raspberry Pi Pico and Pico 2. Based around the RP2040 and RP2350 microcontrollers respectively, Picos are low cost microcontroller device bringing Raspberry Pi quality, cost, and easy of use to the microcontroller space. Jan 2021, Split part in to two versions: tht (this one) and SMD. This one will drill holes for a .1 in header in pcb to allow plugging in the module as well as providing pads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
